# Fritzing sketch Circuit (saved by Fritzing 0.9.3b)
breadboards: 1

parts:
  U3 = RELAY [package=relay-g5q]
  U4 = RELAY [package=relay-g5q]
  V1 = DC Power [voltage=5]
  Raspberry_Pi_Zero1 = Raspberry Pi Zero
  U5 = Voltage Regulator [package=v-reg_dpack]
  TP1 = TP4056 [chip_label=TP4056 package="DIP (Dual Inline) [THT]"]
  L1 = L298
  BAT1 = Battery Holders [package=battery-aa]
  D1 = Diode [package=diode-hv]
  D2 = Diode [package=diode-hv]
  RGB_LED = RGB LED (com. cathode, rgb) [package="5 mm [THT]"]
  PIR_Sensor = HC-SR501 Body Sensor Module
  Camera_servo = Dagu DGServo 9g header connector (female) [package=THT]

nets:
  N1: U3.COIL2, TP1.pin1
  N2: U3.MAIN, TP1.pin6
  N3: U3.NC, U5.OUT, L1.Gnd, D1.A
  N4: U3.COIL1, U4.COIL2
  N5: U4.MAIN, TP1.pin3
  N6: U4.NC, U5.IN, L1.VMS
  N7: U4.COIL1, V1.V+
  GND: V1.V-, Raspberry_Pi_Zero1.GND, D1.C, RGB_LED.common_cathode, PIR_Sensor.GND, Camera_servo.gnd
  N8: Raspberry_Pi_Zero1.GPIO17, RGB_LED.blue_anode
  N9: Raspberry_Pi_Zero1.GPIO27, PIR_Sensor.OUT
  N10: Raspberry_Pi_Zero1.GPIO16, RGB_LED.green_anode
  N11: Raspberry_Pi_Zero1.GPIO18, Camera_servo.pulse
  N12: Raspberry_Pi_Zero1.GPIO15, RGB_LED.red_anode
  VCC: Raspberry_Pi_Zero1.5V, TP1.pin2, D2.C, PIR_Sensor.VCC, Camera_servo.Vcc
  N13: U5.ADJ, D2.A
  N14: TP1.pin4, BAT1.+
  N15: TP1.pin5, BAT1.-

custom parts:
  TP4056: A DIP stand-in part for whatever IC you want. With 6 pins on a 300mil dual inline package (DIP) footprint.
  L298: L298 module
  HC-SR501 Body Sensor Module: Pyroelectric Infrared PIR Motion Sensor Detector Module
