# Fritzing sketch Power Mgmnt (saved by Fritzing 0.9.3b)
circuit board: 10cm x 7cm
breadboards: 1

parts:
  7_2v_Out = Header 2 [package=screwterminal-3.5mm-2_lock]
  5v_In = Header 2 [package=screwterminal-3.5mm-2_lock]
  18650_Ctrl_2 = TP4056 [chip_label=TP4056 package="DIP (Dual Inline) [THT]"]
  Part1 = songle relay
  18650_Ctrl_1 = TP4056 [chip_label=TP4056 package="DIP (Dual Inline) [THT]"]
  BAT1 = 18650 battery holder [package=battery-18650-kit]
  BAT2 = 18650 battery holder [package=battery-18650-kit]

nets:
  N1: 7_2v_Out.1, Part1.COMMON
  N2: 7_2v_Out.2, 18650_Ctrl_1.pin6
  N3: 5v_In.1, 18650_Ctrl_2.pin1, Part1.VCC, 18650_Ctrl_1.pin1
  N4: 5v_In.2, 18650_Ctrl_2.pin2, Part1.GND, 18650_Ctrl_1.pin2
  N5: 18650_Ctrl_2.pin3, Part1.NC
  N6: 18650_Ctrl_2.pin4, BAT2.+
  N7: 18650_Ctrl_2.pin5, BAT2.-
  N8: 18650_Ctrl_2.pin6, 18650_Ctrl_1.pin3
  N9: 18650_Ctrl_1.pin4, BAT1.+
  N10: 18650_Ctrl_1.pin5, BAT1.-

custom parts:
  TP4056: A DIP stand-in part for whatever IC you want. With 6 pins on a 300mil dual inline package (DIP) footprint.
  18650 battery holder: 18650 Battery Holder
